# Fritzing sketch 03_Ender-3-S1-Pro, LED BAR electronic switch (saved by Fritzing 0.9.10b)
breadboards: 1

parts:
  Q1 = NPN-Transistor [mn=BC548C package="TO92 [THT]"]
  R1 = Resistor [tolerance=±5% power=0.25 resistance=10k package=THT]
  R2 = Resistor [tolerance=±5% power=0.25 resistance=4.7k package=THT]
  R3 = Resistor [tolerance=±5% power=0.25 resistance=220 package=THT]
  R4 = Resistor [tolerance=±5% power=0.25 resistance=10k package=THT]
  PC817 = Sharp PC817 [part_number=Q2 package=THT]
  J4 = male pin header, 2 pins [form="♂ (male)" mn=+24V part_number="LED bar" mpn=GND]
  J1 = male pin header, 2 pins [form="♂ (male)" mn=GND mpn=+3.3V part_number=RPi]
  J3 = male pin header, 2 pins [form="♂ (male)" mn=GND mpn=+24V part_number="3D printer"]
  Q3 = Basic FET N-Channel [mn=IRF540N package="TO220 [THT]"]
  J2 = male pin header, 1 pin [form="♂ (male)" mpn=RPi mn=GPIO]

nets:
  N1: Q1.E, R1.Pin_1, R4.Pin_0, J1.pin1, J3.pin1, Q3.source
  N2: Q1.B, R1.Pin_0, R2.Pin_1
  N3: Q1.C, PC817.Pin_2
  N4: R2.Pin_0, J2.pin1
  3.3V: R3.Pin_0, J1.pin2
  N5: R3.Pin_1, PC817.Pin_1
  N6: R4.Pin_1, PC817.Pin_3, Q3.gate
  24V: PC817.Pin_4, J4.pin1, J3.pin2
  N7: J4.pin2, Q3.drain

notes:
  24V z 3D tiskárny
  původní přípojné místo
  3,3V z Raspberry Pi
